# Fritzing sketch final assignment fitzing (saved by Fritzing 0.9.3b)

parts:
  A1 = DHT22 module
  J2 = Basic Servo  # not connected
  Grove1 = Grove OLED 128x96
  A2 = MH-FMD buzzer
  YL-83_-_Control_Board1 = YL-83 Rain Sensor - Control Board
  YL-83_-_Detection_Board1 = YL-83 Rain Sensor - Detection Board
  U3 = Header 1 [package=1x01_offset]
  U6 = Header 1 [package=1x01_offset]  # not connected
  CPU6 = NodeMCU WROOM ESP 32
  U8 = Header 1 [package=1x01_offset]  # not connected
  + = Header 12 [package=1x12_machine-pin-header_lock.004]
  Data = Header 12 [package=1x12_machine-pin-header_lock.004]
  GND = Header 12 [package=1x12_machine-pin-header_lock.004]
  +_2 = Header 12 [package=1x12_machine-pin-header_lock.004]  # not connected
  Data_2 = Header 12 [package=1x12_machine-pin-header_lock.004]
  GND_2 = Header 12 [package=1x12_machine-pin-header_lock.004]
  VIN = Header 3 [package=molex-1x3_lock]
  3_3_V = Header 3 [package=molex-1x3_lock]
  U9 = Header 1 [package=1x01_offset]
  U10 = Header 1 [package=1x01_offset]
  U11 = Header 1 [package=1x01_offset]
  U12 = Header 1 [package=1x01_offset]
  Data1 = Header 12 [package=1x12_machine-pin-header_lock.004]
  Data2 = Header 12 [package=1x12_machine-pin-header_lock.004]
  U13 = Header 1 [package=1x01_offset]  # not connected
  Sensor1 = TTP223B Capacitive Touch Sensor Module
  Water_Level_Sensor1 = Water Level Sensor
  J3 = Basic Servo  # not connected

nets:
  N1: A1.+, GND.6
  N2: A1.Out, Data1.6
  N3: A1.-, +.6
  N4: Grove1.GND, +.2
  N5: Grove1.VCC, GND.2
  N6: Grove1.SDA, Data1.5
  N7: Grove1.SCL, Data1.2
  N8: A2.Pin_1, GND.7
  N9: A2.Pin_2, Data1.8
  N10: A2.Pin_3, +.7
  N11: YL-83_-_Control_Board1.VCC, Data2.6
  N12: YL-83_-_Control_Board1.GND, GND_2.1
  N13: YL-83_-_Control_Board1.AO, Data2.3
  N14: YL-83_-_Control_Board1.POS, YL-83_-_Detection_Board1.POS
  N15: YL-83_-_Control_Board1.NEG, YL-83_-_Detection_Board1.NEG
  N16: U3.1, CPU6.pin_19
  N17: CPU6.pin_3, Data.1
  N18: CPU6.pin_4, Data.2
  N19: CPU6.pin_5, Data.3
  N20: CPU6.pin_6, Data.4
  N21: CPU6.pin_7, Data.5
  N22: CPU6.pin_8, CPU6.pin_24, CPU6.pin_28, Data.6, Data_2.4, Data_2.8
  N23: CPU6.pin_9, CPU6.pin_25, Data.7, Data_2.7
  N24: CPU6.pin_10, Data.8
  N25: CPU6.pin_11, Data.9
  N26: CPU6.pin_12, Data.10
  N27: CPU6.pin_13, Data.11
  N28: CPU6.pin_14, Data.12
  N29: CPU6.pin_15, U11.1
  N30: CPU6.pin_16, VIN.3
  N31: CPU6.pin_17, 3_3_V.1
  N32: CPU6.pin_18, U9.1
  N33: CPU6.pin_20, Data_2.12
  N34: CPU6.pin_21, Data_2.11
  N35: CPU6.pin_22, Data_2.10
  N36: CPU6.pin_23, Data_2.9
  N37: CPU6.pin_26, Data_2.6
  N38: CPU6.pin_27, Data_2.5
  N39: CPU6.pin_29, Data_2.3
  N40: CPU6.pin_30, Data_2.2
  N41: CPU6.pin_31, Data_2.1
  N42: +.9, Sensor1.GND
  N43: GND.9, Sensor1.VCC
  N44: GND_2.8, Water_Level_Sensor1.GND
  N45: VIN.1, U12.1
  N46: 3_3_V.3, U10.1
  N47: Data1.9, Sensor1.SIG
  N48: Data2.5, Water_Level_Sensor1.VCC
  N49: Data2.10, Water_Level_Sensor1.SIG

custom parts:
  DHT22 module: DHT22 module. Pins VCC Data GND.
  MH-FMD buzzer: MH-FMD buzzer.
  YL-83 Rain Sensor - Control Board: The YL-83 is a rain sensor that has more resistance when dry and less resistance when wet. The module runs at 5V.
  YL-83 Rain Sensor - Detection Board: The YL-83 is a rain sensor that has more resistance when dry and less resistance when wet. The module runs at 5V.
  NodeMCU WROOM ESP 32: 30 pol Development Kit
  TTP223B Capacitive Touch Sensor Module: The TTP223B capacitive touch sensor module uses the TTP223B IC. The appropriate voltage is approximately 2 to 5.5 volts.
  Water Level Sensor: A water level sensor. This sensor operates at 3V to 5V. The Sig (signal) pin outputs an analogue signal that is in proportion to the amount of water in contact with the sensor.
